// Logisim project 1.1.1.circ as structural Verilog: 1 circuit, main circuit main
module main (
  input  A,
  input  B,
  input  A_2,
  input  B_2,
  input  in_5,
  input  A_3,
  input  B_3,
  input  A_4,
  input  B_4,
  input  A_5,
  input  B_5,
  input  A_6,
  input  B_6,
  output AND,
  output OR,
  output out_16,
  output out_17,
  output out_18,
  output out_19,
  output NOR
);

  and and_1 (AND, A, B);
  or or_1 (OR, A_2, B_2);
  not not_1 (out_16, in_5);
  xor xor_1 (out_17, A_3, B_3);
  xnor xnor_1 (out_18, A_4, B_4);
  nand nand_1 (out_19, A_5, B_5);
  nor nor_1 (NOR, A_6, B_6);

  // Notes on the sheet:
  //   NOT
  //   XOR
  //   XNOR
  //   NAND
endmodule
