// Logisim project 1.1.2.circ as structural Verilog: 1 circuit, main circuit main
module main (
  input  in_1,
  input  in_2,
  input  in_3,
  input  in_4,
  input  [7:0] in_5,
  input  in_6,
  input  in_7,
  output out_8,
  output out_9,
  output out_10,
  output out_11,
  output [7:0] out_12
);

  wire clock_1_out, clock_2_out, clock_3_out;

  Clock clock_1 (.out(clock_1_out));
  Clock clock_2 (.out(clock_2_out));
  Clock clock_3 (.out(clock_3_out));
  D_Flip_Flop #(.trigger("high")) d_ff_1 (
    .clk(clock_1_out), .D(in_1), .Q(out_8), .Qn(out_9), .en(in_2));  // open: preset, reset
  D_Flip_Flop d_ff_2 (.clk(clock_2_out), .D(in_3), .Q(out_10), .Qn(out_11), .en(in_4));  // open: preset, reset
  Register register_1 (.D(in_5), .en(in_6), .Q(out_12), .clk(clock_3_out), .clr(in_7));

  // Notes on the sheet:
  //   D-Latch
  //   D-Flip Flop
endmodule
