// Logisim project 1.1.3&1.1.4.circ as structural Verilog: 1 circuit, main circuit main
module main (
  input  A,
  input  B,
  input  C,
  input  A_2,
  input  B_2,
  input  C_2,
  input  D,
  output F,
  output A_o,
  output B_o,
  output C_o,
  output D_o
);

  wire and_1_out, clock_1_out;

  Clock clock_1 (.out(clock_1_out));
  and and_1 (and_1_out, A, B);
  or or_1 (F, and_1_out, C);
  Register #(.width(4)) register_1 (
    .D({D, C_2, B_2, A_2}), .en(1'b1), .Q({D_o, C_o, B_o, A_o}), .clr(clock_1_out));  // open: clk

  // Notes on the sheet:
  //   clock
endmodule
