// Logisim project 2.2.circ as structural Verilog: 1 circuit, main circuit main
module main (
);

  D_Flip_Flop #(.trigger("high")) d_ff_1 ();  // open: clk, D, Q, Qn, preset, en, reset
  D_Flip_Flop d_ff_2 ();  // open: clk, D, Q, Qn, preset, en, reset
  Register register_1 ();  // open: D, en, Q, clk, clr

  // Notes on the sheet:
  //   D Latch
  //   D Flip Flop
  //   Thanh ghi
endmodule
