// Logisim project 19520208_Lab2_2.1.circ as structural Verilog: 1 circuit, main circuit main
module main (
  input  [1:0] in_1,
  input  [7:0] in_2,
  input  [7:0] in_3,
  output [7:0] Output
);

  wire [7:0] adder_1_out, AND_out, NAND_out, subtractor_1_out;

  Adder adder_1 (.a(in_2), .b(in_3), .out(adder_1_out));  // open: cin, cout
  Subtractor subtractor_1 (.a(in_2), .b(in_3), .out(subtractor_1_out));  // open: bin, bout
  assign AND_out = in_2 & in_3;  // AND_Gate AND, 8 bits wide
  assign NAND_out = ~(in_2 & in_3);  // NAND_Gate NAND, 8 bits wide
  Multiplexer #(.select(2), .width(8)) multiplexer_1 (
    .in0(adder_1_out), .in1(subtractor_1_out), .in2(AND_out), .in3(NAND_out), .out(Output), .sel(in_1));  // open: en

  // Notes on the sheet:
  //   A
  //   B
  //   Ngõ vào điều khiển
  //   S
endmodule
