// Logisim project 19520208_Lab2_3.1.circ as structural Verilog: 1 circuit, main circuit main
module main (
  input  [7:0] in_1,
  input  [2:0] in_2,
  input  [7:0] in_3,
  input  [7:0] in_4,
  output [7:0] out_5
);

  wire [7:0] adder_1_out, adder_2_out, and_1_out, not_1_out, or_1_out, subtractor_1_out, subtractor_2_out,
       xor_1_out;

  Adder adder_1 (.a(in_1), .b(in_3), .out(adder_1_out));  // open: cin, cout
  Adder adder_2 (.a(in_1), .b(in_4), .out(adder_2_out));  // open: cin, cout
  Subtractor subtractor_1 (.a(in_1), .b(in_3), .out(subtractor_1_out));  // open: bin, bout
  Subtractor subtractor_2 (.a(in_1), .b(in_4), .out(subtractor_2_out));  // open: bin, bout
  assign and_1_out = in_1 & in_3;  // AND_Gate and_1, 8 bits wide
  assign or_1_out = in_1 | in_3;  // OR_Gate or_1, 8 bits wide
  assign not_1_out = ~in_1;  // NOT_Gate not_1, 8 bits wide
  assign xor_1_out = in_1 ^ in_3;  // XOR_Gate xor_1, 8 bits wide
  Multiplexer #(.select(3), .width(8)) multiplexer_1 (
    .in0(adder_1_out), .in1(adder_2_out), .in2(subtractor_1_out), .in3(subtractor_2_out), .in4(and_1_out),
    .in5(or_1_out), .in6(not_1_out), .in7(xor_1_out), .out(out_5), .sel(in_2));  // open: en

  // Notes on the sheet:
  //   A
  //   B
  //   1
  //   A+1
  //   A-B
  //   A-1
  //   NOT A
  //   A+B
  //   A AND B
  //   A OR B
  //   A XOR B
endmodule
